# Fritzing sketch PillNow_arduino_fritzing (saved by Fritzing 0.9.3b)

parts:
  R1 = PHOTOCELL [package=photocell]
  부품1 = Arduino Nano (Rev3.0)
  R2 = Resistor [tolerance=±0.05% resistance=10k package="0402 [SMD]"]
  BT1 = Bluetooth HC-06u [package=THT]

nets:
  N1: R1.P$1, 부품1.A0, R2.Pin_1
  GND: R1.P$2, 부품1.GND, BT1.GND
  N2: 부품1.D2, BT1.RXD
  N3: 부품1.D3, BT1.TXD
  5V: 부품1.5V, R2.Pin_0, BT1.VCC

custom parts:
  Bluetooth HC-06u: Bluetooth HC-06 - face up, pins down 16.5mm x 37.5mm PCB
